# Fritzing sketch RPi.BMP180 (saved by Fritzing 0.9.3b)
breadboards: 1

parts:
  Raspberry_Pi_1 = Raspberry Pi 3 [part_number=RPI-3-V1.2]
  Part2 = Adafruit BMP180

nets:
  3V3: Raspberry_Pi_1.3v3, Part2.+3V3
  N1: Raspberry_Pi_1.GPIO2, Part2.SDA
  N2: Raspberry_Pi_1.GPIO3, Part2.SCL
  GND: Raspberry_Pi_1.GND, Part2.GND

custom parts:
  Adafruit BMP180: This precision sensor from Bosch is the best low-cost sensing solution for measuring barometric pressure and temperature. Because pressure changes with altitude you can also use it as an altimeter! The sensor is soldered onto a PCB with a 3.3V regulator, I2C level shifter and pull-up resistors on the I2C pins. The BMP180 is the next-generation of sensors from Bosch, and replaces the BMP085.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
