# Fritzing sketch RPi.HMC5883L (saved by Fritzing 0.9.3b)
breadboards: 1

parts:
  Raspberry_Pi_1 = Raspberry Pi 3 [part_number=RPI-3-V1.2]
  Part1 = Triple Axis Magnetometer - HMC5883 Breakout

nets:
  3V3: Raspberry_Pi_1.3v3, Part1.VCC
  N1: Raspberry_Pi_1.GPIO2, Part1.SDA
  N2: Raspberry_Pi_1.GPIO3, Part1.SCL
  GND: Raspberry_Pi_1.GND, Part1.GND
