# Fritzing sketch RPi.PCA9685 (saved by Fritzing 0.9.3b)
breadboards: 1

parts:
  Part1 = 16-Channel 12-bit PWM Servo Driver - I2C [part_number=815]
  J1 = Basic Servo
  Raspberry_Pi_1 = Raspberry Pi 3 [part_number=RPI-3-V1.2]

nets:
  GND: Part1.GND, J1.gnd, Raspberry_Pi_1.GND
  VCC: Part1.VCC, Raspberry_Pi_1.3v3
  N1: Part1.5.0V, J1.pulse
  N2: Part1.SDA, Raspberry_Pi_1.GPIO2
  N3: Part1.SCL, Raspberry_Pi_1.GPIO3
  N4: Part1.PWM15, J1.vcc

notes:
  5V power
  supply

custom parts:
  16-Channel 12-bit PWM Servo Driver - I2C: You want to make a cool robot, maybe a hexapod walker, or maybe just a piece of art with a lot of moving parts. Or maybe you want to drive a lot of LEDs with precise PWM output. Using only two pins, control 16 free-running PWM outputs! You can even chain up 62 breakouts to control up to 992 PWM outputs.
