# Fritzing sketch RPi.SSD1306.MCP3008 (saved by Fritzing 0.9.3b)
breadboards: 1

parts:
  Part1 = OLED Monochrome 128x32 I2C [part_number=931]
  Raspberry_Pi_1 = Raspberry Pi 3 [part_number=RPI-3-V1.2]
  IC1 = MCP3008 8-channel 10-bit ADC [part_number=MCP3008]
  U1 = POT [package=3362u]

nets:
  3.3V: Part1.3.3V, Raspberry_Pi_1.3v3, IC1.no_name_yet#15, IC1.no_name_yet#16, U1.E
  GND: Part1.GND, Raspberry_Pi_1.GND, IC1.no_name_yet#9, IC1.no_name_yet#14, U1.A
  N1: Part1.SCL, Raspberry_Pi_1.GPIO3
  N2: Part1.SDA, Raspberry_Pi_1.GPIO2
  N3: Raspberry_Pi_1.GPIO10, IC1.no_name_yet#11
  N4: Raspberry_Pi_1.GPIO9, IC1.no_name_yet#12
  N5: Raspberry_Pi_1.GPIO11, IC1.no_name_yet#13
  N6: Raspberry_Pi_1.GPIO8, IC1.no_name_yet#10
  N7: IC1.no_name_yet#1, U1.S

custom parts:
  OLED Monochrome 128x32 I2C: These displays are small, only about 1" diagonal, but very readable due to the high contrast of an OLED display. This display is made of 128x32 individual white OLED pixels, each one is turned on or off by the controller chip. Because the display makes its own light, no backlight is required. This reduces the power required to run the OLED and is why the display has such high contrast; we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
