# Fritzing sketch RPi.SSD1306 (saved by Fritzing 0.9.3b)
breadboards: 1

parts:
  Part1 = OLED Monochrome 128x32 I2C [part_number=931]
  Raspberry_Pi_1 = Raspberry Pi 3 [part_number=RPI-3-V1.2]

nets:
  3.3V: Part1.3.3V, Raspberry_Pi_1.3v3
  GND: Part1.GND, Raspberry_Pi_1.GND
  N1: Part1.SCL, Raspberry_Pi_1.GPIO3
  N2: Part1.SDA, Raspberry_Pi_1.GPIO2

custom parts:
  OLED Monochrome 128x32 I2C: These displays are small, only about 1" diagonal, but very readable due to the high contrast of an OLED display. This display is made of 128x32 individual white OLED pixels, each one is turned on or off by the controller chip. Because the display makes its own light, no backlight is required. This reduces the power required to run the OLED and is why the display has such high contrast; we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
