# Fritzing sketch RPi.TSL2561 (saved by Fritzing 0.9.3b)
breadboards: 1

parts:
  Part1 = Adafruit TSL2561 [part_number="Adafruit #439"]
  Raspberry_Pi_1 = Raspberry Pi 3 [part_number=RPI-3-V1.2]

nets:
  GND: Part1.GND, Raspberry_Pi_1.GND
  3.3V: Part1.3.3V, Raspberry_Pi_1.3v3
  N1: Part1.SDA, Raspberry_Pi_1.GPIO2
  N2: Part1.SCL, Raspberry_Pi_1.GPIO3

custom parts:
  Adafruit TSL2561: The TSL2561 luminosity sensor is an advanced digital light sensor, ideal for use in a wide range of light situations. Compared to low cost CdS cells, this sensor is more precise, allowing for exact lux calculations and can be configured for different gain/timing ranges to detect light ranges from up to 0.1 - 40,000+ Lux on the fly. The best part of this sensor is that it contains both infrared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
