# Fritzing sketch RaspberryPI.STH10 (saved by Fritzing 0.9.3b)
breadboards: 1

parts:
  R1 = Resistor [tolerance=±5% resistance=10k package=THT]
  Raspberry_Pi_1 = Raspberry Pi 3 [part_number=RPI-3-V1.2]
  U1 = SHT1x Humdity Sensor [package=sht1x]

nets:
  N1: R1.Pin_0, Raspberry_Pi_1.GPIO18, U1.DATA
  3V3: R1.Pin_1, Raspberry_Pi_1.3v3, U1.VDD
  N2: Raspberry_Pi_1.GPIO23, U1.SCK
  GND: Raspberry_Pi_1.GND, U1.GND

notes:
  Here go the connectors of the STH10. Yellow: SCL, blue: SDA, red: VCC and green: GND wires.
